// Logisim project ControlUnit.circ as structural Verilog: 10 circuits, main circuit -OpDecoder-
module ControlUnit (
  input  [5:0] OpCode,
  input  [5:0] FunCode,
  input  Start,
  input  Clk,
  input  Rst,
  input  ZF,
  input  NF,
  input  RF
);

  wire and_1_out, and_2_out, and_3_out, and_4_out, and_5_out, and_6_out, and_7_out, comparator_2_lt,
       comparator_3_eq, comparator_4_eq, comparator_5_lt, demultiplexer_1_out0, demultiplexer_1_out1, EALU1,
       EALU2, EALU10, EALU11, EB0, EB1, EB2, EB4, EB10, EB11, EBj, ED, EHi2, EI, EJ, ELo2, End, End0, End4,
       END_q, Endj, EO2, EO_2, EO_2_t, EPC0, EPC4, EPC11, EPCj, ER1, ER2, ER4, ER10, ER11, ERb, ERs, EW1,
       EW3, EW10, IDLE_q, IOp, jr, mfhi, mflo, nop, or_1_out, or_2_out, or_5_out, PC1, PC2, PC3, PC10, PCnop,
       SIS, SPC, SWA10, VOp;
  wire [1:0] OpType, SA0, SA1, SA2, SA4, SA10, SA11, SAj, SB0, SB1, SB2, SB4, SB10, SB11, SBj, SW1, SW3, SW10;
  wire [3:0] OpS, SALU0, SALU1, SALU2, SALU4, SALU10, SALU11, SALUj;

  OpDecoder opdecoder_1 (
    .OpCode(OpCode), .FunCode(FunCode),
    .Type__0_for_basic_type_R__and_1_for_special_R__2_for_type_I_and_3_for_type_J(OpType),
    .OpS__Selector_of_the_operation(OpS), .Valid__1_if_the_OC_and_FC_belong_to_a_valid_operation(VOp));
  Decoder #(.select(2), .disabled(0)) decoder_1 (.out0(ERb), .out1(ERs), .out2(EI), .out3(EJ), .sel(OpType), .en(ED));
  Decoder #(.select(2), .disabled(0)) decoder_2 (
    .out0(mfhi), .out1(mflo), .out2(nop), .out3(jr), .sel(OpS[1:0]), .en(EO_2_t));
  Demultiplexer #(.disabled(0), .enable("false")) demultiplexer_1 (
    .out0(demultiplexer_1_out0), .out1(demultiplexer_1_out1), .in(IDLE_q), .sel(Start));
  D_Flip_Flop IDLE (.clk(Clk), .D(or_1_out), .Q(IDLE_q), .preset(Rst));  // open: Qn, en, reset
  or or_1 (or_1_out, demultiplexer_1_out0, IOp);
  D_Flip_Flop u_END (.clk(Clk), .D(End), .Q(END_q), .reset(Rst));  // open: Qn, preset, en
  Comparator #(.width(2), .mode("unsigned")) comparator_1 (.a(2'b10), .b(OpS[3:2]), .gt(EO_2), .eq(EO2), .lt(EO_2_t));
  Demultiplexer #(.disabled(0), .enable("false")) demultiplexer_2 (.out0(IOp), .out1(ED), .in(or_2_out), .sel(VOp));
  or or_2 (or_2_out, demultiplexer_1_out1, END_q);
  or or_3 (End, End0, Endj);
  buf or_4 (SPC, PC1);  // OR_Gate
  D_Flip_Flop u_SPC (.clk(Clk), .D(SPC), .Q(PCnop), .reset(Rst));  // open: Qn, preset, en
  Comparator #(.width(4), .mode("unsigned")) comparator_2 (.a(4'b0110), .b(OpS), .lt(comparator_2_lt));  // open: gt, eq
  and and_1 (and_1_out, comparator_2_lt, ERb);
  or or_5 (or_5_out, PCnop, and_2_out);
  and and_2 (and_2_out, ERb, nop);
  and and_3 (and_3_out, EO_2, ERb);
  and and_4 (and_4_out, EO2, ERb);
  Comparator #(.width(3), .mode("unsigned")) comparator_3 (
    .a(OpS[3:1]), .b(3'b110), .eq(comparator_3_eq));  // open: gt, lt
  Comparator #(.width(4), .mode("unsigned")) comparator_4 (.a(4'b1111), .b(OpS), .eq(comparator_4_eq));  // open: gt, lt
  IALU ialu_1 (
    .Start(and_1_out), .Clk(Clk), .Rst(Rst), .SALU(OpS), .ER(ER10), .SA(SA10), .SB(SB10), .EB(EB10),
    .SWA(SWA10), .SIS(SIS), .SALU_2(SALU10), .EALU(EALU10), .SW(SW10), .EW(EW10), .End(PC10));
  Comparator #(.width(4), .mode("unsigned")) comparator_5 (.a(4'b0110), .b(OpS), .lt(comparator_5_lt));  // open: gt, eq
  nop nop_1 (
    .Start(or_5_out), .Clk(Clk), .Rst(Rst), .SA(SA0), .SB(SB0), .EB(EB0), .SALU(SALU0), .EPC(EPC0), .End(End0));
  RbALUResult rbaluresult_1 (
    .Start(and_3_out), .Clk(Clk), .Rst(Rst), .SALU(OpS), .ER(ER1), .SA(SA1), .SB(SB1), .EB(EB1),
    .SALU_2(SALU1), .EALU(EALU1), .SW(SW1), .EW(EW1), .End(PC1));
  RbALULoHi rbalulohi_1 (
    .Start(and_4_out), .Clk(Clk), .Rst(Rst), .SALU(OpS), .SA(SA2), .SB(SB2), .EB(EB2), .ER(ER2),
    .SALU_2(SALU2), .EALU(EALU2), .EHi(EHi2), .ELo(ELo2), .End(PC2));
  RbMfhi_lo rbmfhi_lo_1 (.Start(and_5_out), .Clk(Clk), .Rst(Rst), .SOp(OpS), .SW(SW3), .EW(EW3), .End(PC3));
  and and_5 (and_5_out, comparator_3_eq, ERb);
  jr jr_1 (
    .Start(and_6_out), .Clk(Clk), .Rst(Rst), .SA(SA4), .SB(SB4), .EB(EB4), .ER(ER4), .SALU(SALU4),
    .EPC(EPC4), .End(End4));
  and and_6 (and_6_out, comparator_4_eq, ERb);
  Ibf ibf_1 (
    .Start(and_7_out), .Clk(Clk), .Rst(Rst), .OS(OpS), .ZF(ZF), .NF(NF), .ER(ER11), .SA(SA11), .SB(SB11),
    .EB(EB11), .SALU(SALU11), .EALU(EALU11), .EPC(EPC11));  // open: End
  and and_7 (and_7_out, comparator_5_lt, ERb);
  j j_1 (.Start(EJ), .Clk(Clk), .Rst(Rst), .SA(SAj), .SB(SBj), .EB(EBj), .SALU(SALUj), .EPC(EPCj), .End(Endj));

  // Other names for the same wires on the sheet: FC[5:0] = FunCode; OC[5:0] = OpCode; SO[1:0] = OpS[1:0]; St = Start

  // Notes on the sheet:
  //   Input
  //   Output
  //   Initial Circuit
  //   Selector Decoder
  //   End Instruction
  //   Save PC Instruction
  //   Machines
  //   Cambiar numeros
endmodule

module OpDecoder (
  input  [5:0] OpCode,
  input  [5:0] FunCode,
  output [1:0] Type__0_for_basic_type_R__and_1_for_special_R__2_for_type_I_and_3_for_type_J,
  output [3:0] OpS__Selector_of_the_operation,
  output Valid__1_if_the_OC_and_FC_belong_to_a_valid_operation
);

  wire and_1_out, and_2_out, and_3_out, comparator_5_eq, comparator_6_eq, comparator_7_eq, comparator_8_eq,
       comparator_9_eq, comparator_10_eq, comparator_11_eq, comparator_12_eq, comparator_13_eq,
       comparator_14_eq, comparator_15_eq, comparator_16_eq, comparator_17_eq, comparator_18_eq,
       comparator_19_eq, comparator_20_eq, comparator_21_eq, comparator_22_eq, comparator_23_eq,
       comparator_24_eq, comparator_25_eq, comparator_26_eq, comparator_27_eq, comparator_28_eq,
       comparator_29_eq, comparator_30_eq, comparator_31_eq, comparator_32_eq, comparator_33_eq,
       comparator_34_eq, comparator_35_eq, comparator_36_eq, comparator_37_eq, comparator_38_eq,
       comparator_39_eq, I, J, multiplexer_1_out, multiplexer_2_out, multiplexer_3_out, multiplexer_4_out,
       multiplexer_5_out, multiplexer_6_out, Rb, Rs, Rs0, Rs1, VI, VRb, VRs;
  wire [3:0] OpSI, OpSJ, OpSRb, OpSRs;

  Comparator #(.width(6)) comparator_1 (.a(OpCode), .b(6'b000010), .eq(J));  // open: gt, lt
  Comparator #(.width(6)) comparator_2 (.a(OpCode), .b({6{1'b0}}), .eq(Rb));  // open: gt, lt
  Comparator #(.width(6)) comparator_3 (.a(OpCode), .b(6'b111000), .eq(Rs0));  // open: gt, lt
  Comparator #(.width(6)) comparator_4 (.a(OpCode), .b({6{1'b1}}), .eq(Rs1));  // open: gt, lt
  or or_1 (Rs, Rs0, Rs1);
  nor nor_1 (I, Rb, Rs, J);
  Priority_Encoder #(.select(2)) priority_encoder_1 (
    .in0(Rb), .in1(Rs), .in2(I), .in3(J),
    .out(Type__0_for_basic_type_R__and_1_for_special_R__2_for_type_I_and_3_for_type_J));  // open: gs, en_out, en_in
  Comparator #(.width(6)) comparator_5 (.a(FunCode), .b(6'b100000), .eq(comparator_5_eq));  // open: gt, lt
  Comparator #(.width(6)) comparator_6 (.a(FunCode), .b(6'b100010), .eq(comparator_6_eq));  // open: gt, lt
  Comparator #(.width(6)) comparator_7 (.a(FunCode), .b(6'b100100), .eq(comparator_7_eq));  // open: gt, lt
  Comparator #(.width(6)) comparator_8 (.a(FunCode), .b(6'b100101), .eq(comparator_8_eq));  // open: gt, lt
  Comparator #(.width(6)) comparator_9 (.a(FunCode), .b(6'b100111), .eq(comparator_9_eq));  // open: gt, lt
  Comparator #(.width(6)) comparator_10 (.a(FunCode), .b(6'b101000), .eq(comparator_10_eq));  // open: gt, lt
  Comparator #(.width(6)) comparator_11 (.a(FunCode), .b(6'b101010), .eq(comparator_11_eq));  // open: gt, lt
  Comparator #(.width(6)) comparator_12 (.a(FunCode), .b(6'b101011), .eq(comparator_12_eq));  // open: gt, lt
  Comparator #(.width(6)) comparator_13 (.a(FunCode), .b(6'b011000), .eq(comparator_13_eq));  // open: gt, lt
  Comparator #(.width(6)) comparator_14 (.a(FunCode), .b(6'b011001), .eq(comparator_14_eq));  // open: gt, lt
  Comparator #(.width(6)) comparator_15 (.a(FunCode), .b(6'b011010), .eq(comparator_15_eq));  // open: gt, lt
  Comparator #(.width(6)) comparator_16 (.a(FunCode), .b(6'b011011), .eq(comparator_16_eq));  // open: gt, lt
  Comparator #(.width(6)) comparator_17 (.a(FunCode), .b(6'b010000), .eq(comparator_17_eq));  // open: gt, lt
  Comparator #(.width(6)) comparator_18 (.a(FunCode), .b(6'b010010), .eq(comparator_18_eq));  // open: gt, lt
  Comparator #(.width(6)) comparator_19 (.a(FunCode), .b({6{1'b0}}), .eq(comparator_19_eq));  // open: gt, lt
  Comparator #(.width(6)) comparator_20 (.a(FunCode), .b(6'b001000), .eq(comparator_20_eq));  // open: gt, lt
  Multiplexer #(.disabled(0), .enable("false")) multiplexer_1 (
    .in0(1'b0), .in1(comparator_21_eq), .out(multiplexer_1_out), .sel(Rs0));
  Comparator #(.width(6)) comparator_21 (.a(FunCode), .b({6{1'b0}}), .eq(comparator_21_eq));  // open: gt, lt
  Multiplexer #(.disabled(0), .enable("false")) multiplexer_2 (
    .in0(1'b0), .in1(comparator_22_eq), .out(multiplexer_2_out), .sel(Rs0));
  Comparator #(.width(6)) comparator_22 (.a(FunCode), .b(6'b000001), .eq(comparator_22_eq));  // open: gt, lt
  Multiplexer #(.disabled(0), .enable("false")) multiplexer_3 (
    .in0(1'b0), .in1(comparator_23_eq), .out(multiplexer_3_out), .sel(Rs1));
  Comparator #(.width(6)) comparator_23 (.a(FunCode), .b({6{1'b1}}), .eq(comparator_23_eq));  // open: gt, lt
  Multiplexer #(.disabled(0), .enable("false")) multiplexer_4 (
    .in0(1'b0), .in1(comparator_24_eq), .out(multiplexer_4_out), .sel(Rs1));
  Comparator #(.width(6)) comparator_24 (.a(FunCode), .b(6'b000010), .eq(comparator_24_eq));  // open: gt, lt
  Multiplexer #(.disabled(0), .enable("false")) multiplexer_5 (
    .in0(1'b0), .in1(comparator_25_eq), .out(multiplexer_5_out), .sel(Rs1));
  Comparator #(.width(6)) comparator_25 (.a(FunCode), .b(6'b000100), .eq(comparator_25_eq));  // open: gt, lt
  Multiplexer #(.disabled(0), .enable("false")) multiplexer_6 (
    .in0(1'b0), .in1(comparator_26_eq), .out(multiplexer_6_out), .sel(Rs1));
  Comparator #(.width(6)) comparator_26 (.a(FunCode), .b(6'b000001), .eq(comparator_26_eq));  // open: gt, lt
  Priority_Encoder #(.select(4), .disabled(0)) priority_encoder_2 (
    .in0(comparator_5_eq), .in1(comparator_6_eq), .in2(comparator_7_eq), .in3(comparator_8_eq),
    .in4(comparator_9_eq), .in5(comparator_10_eq), .in6(comparator_11_eq), .in7(comparator_12_eq),
    .in8(comparator_13_eq), .in9(comparator_14_eq), .in10(comparator_15_eq), .in11(comparator_16_eq),
    .in12(comparator_17_eq), .in13(comparator_18_eq), .in14(comparator_19_eq), .in15(comparator_20_eq),
    .out(OpSRb), .gs(VRb), .en_in(Rb));  // open: en_out
  Priority_Encoder #(.select(4), .disabled(0)) priority_encoder_3 (
    .in0(multiplexer_1_out), .in1(multiplexer_2_out), .in2(multiplexer_3_out), .in3(multiplexer_4_out),
    .in4(multiplexer_5_out), .in5(multiplexer_6_out), .in6(1'b0), .in7(1'b0), .in8(1'b0), .in9(1'b0),
    .in10(1'b0), .in11(1'b0), .in12(1'b0), .in13(1'b0), .in14(1'b0), .in15(1'b0), .out(OpSRs), .gs(VRs),
    .en_in(Rs));  // open: en_out
  and and_1 (and_1_out, Rb, VRb);
  and and_2 (and_2_out, Rs, VRs);
  and and_3 (and_3_out, I, VI);
  or or_2 (Valid__1_if_the_OC_and_FC_belong_to_a_valid_operation, J, and_1_out, and_2_out, and_3_out);
  Comparator #(.width(6)) comparator_27 (.a(OpCode), .b(6'b001000), .eq(comparator_27_eq));  // open: gt, lt
  Comparator #(.width(6)) comparator_28 (.a(OpCode), .b(6'b001010), .eq(comparator_28_eq));  // open: gt, lt
  Comparator #(.width(6)) comparator_29 (.a(OpCode), .b(6'b001011), .eq(comparator_29_eq));  // open: gt, lt
  Comparator #(.width(6)) comparator_30 (.a(OpCode), .b(6'b001100), .eq(comparator_30_eq));  // open: gt, lt
  Comparator #(.width(6)) comparator_31 (.a(OpCode), .b(6'b001101), .eq(comparator_31_eq));  // open: gt, lt
  Comparator #(.width(6)) comparator_32 (.a(OpCode), .b(6'b001110), .eq(comparator_32_eq));  // open: gt, lt
  Comparator #(.width(6)) comparator_33 (.a(OpCode), .b(6'b000100), .eq(comparator_33_eq));  // open: gt, lt
  Comparator #(.width(6)) comparator_34 (.a(OpCode), .b(6'b000101), .eq(comparator_34_eq));  // open: gt, lt
  Comparator #(.width(6)) comparator_35 (.a(OpCode), .b(6'b000110), .eq(comparator_35_eq));  // open: gt, lt
  Comparator #(.width(6)) comparator_36 (.a(OpCode), .b(6'b000111), .eq(comparator_36_eq));  // open: gt, lt
  Comparator #(.width(6)) comparator_37 (.a(OpCode), .b(6'b000001), .eq(comparator_37_eq));  // open: gt, lt
  Comparator #(.width(6)) comparator_38 (.a(OpCode), .b(6'b100011), .eq(comparator_38_eq));  // open: gt, lt
  Comparator #(.width(6)) comparator_39 (.a(OpCode), .b(6'b101011), .eq(comparator_39_eq));  // open: gt, lt
  Pull_Resistor pull_resistor_1 (.node(OpSRb));
  Pull_Resistor pull_resistor_2 (.node(OpSRs));
  Pull_Resistor pull_resistor_3 (.node(OpSI));
  Pull_Resistor pull_resistor_4 (.node(OpSJ));
  assign OpS__Selector_of_the_operation = OpSRb | OpSRs | OpSI | OpSJ;  // OR_Gate or_3, 4 bits wide
  Priority_Encoder #(.select(4), .disabled(0)) priority_encoder_4 (
    .in0(comparator_27_eq), .in1(comparator_28_eq), .in2(comparator_29_eq), .in3(comparator_30_eq),
    .in4(comparator_31_eq), .in5(comparator_32_eq), .in6(comparator_33_eq), .in7(comparator_34_eq),
    .in8(comparator_35_eq), .in9(comparator_36_eq), .in10(comparator_37_eq), .in11(comparator_38_eq),
    .in12(comparator_39_eq), .in13(1'b0), .in14(1'b0), .in15(1'b0), .out(OpSI), .gs(VI), .en_in(I));  // open: en_out

  // Other names for the same wires on the sheet: FC[5:0] = FunCode; OC[5:0] = OpCode;
  //   OpS[3:0] = OpS__Selector_of_the_operation;
  //   Type[1:0] = Type__0_for_basic_type_R__and_1_for_special_R__2_for_type_I_and_3_for_type_J;
  //   Valid = Valid__1_if_the_OC_and_FC_belong_to_a_valid_operation
endmodule

module RbALUResult (
  input  Start,
  input  Clk,
  input  Rst,
  input  [3:0] SALU,
  output ER,
  output [1:0] SA,
  output [1:0] SB,
  output EB,
  output [3:0] SALU_2,
  output EALU,
  output [1:0] SW,
  output EW,
  output End
);

  Multiplexer #(.width(2), .disabled(0), .enable("false")) multiplexer_1 (
    .in0(2'b00), .in1(2'b01), .out(SA), .sel(Start));
  Multiplexer #(.width(2), .disabled(0), .enable("false")) multiplexer_2 (
    .in0(2'b00), .in1(2'b01), .out(SB), .sel(Start));
  Multiplexer #(.width(4), .disabled(0), .enable("false")) multiplexer_3 (
    .in0(4'b0000), .in1(SALU), .out(SALU_2), .sel(Start));

  assign EALU = Start;
  assign EB = Start;
  assign End = Start;
  assign ER = Start;
  assign EW = Start;
  assign SW = 2'b00;

  // Other names for the same wires on the sheet: St = Start

  // Notes on the sheet:
  //   Input
  //   Ground
  //   Output
endmodule

module RbALULoHi (
  input  Start,
  input  Clk,
  input  Rst,
  input  [3:0] SALU,
  output [1:0] SA,
  output [1:0] SB,
  output EB,
  output ER,
  output [3:0] SALU_2,
  output EALU,
  output EHi,
  output ELo,
  output End
);

  Multiplexer #(.width(2), .disabled(0), .enable("false")) multiplexer_1 (
    .in0(2'b00), .in1(2'b01), .out(SA), .sel(Start));
  Multiplexer #(.width(2), .disabled(0), .enable("false")) multiplexer_2 (
    .in0(2'b00), .in1(2'b01), .out(SB), .sel(Start));

  assign EALU = Start;
  assign EB = Start;
  assign EHi = Start;
  assign ELo = Start;
  assign End = Start;
  assign ER = Start;
  assign SALU_2 = SALU;

  // Other names for the same wires on the sheet: St = Start

  // Notes on the sheet:
  //   Input
  //   Ground
  //   Output
endmodule

module nop (
  input  Start,
  input  Clk,
  input  Rst,
  output [1:0] SA,
  output [1:0] SB,
  output EB,
  output [3:0] SALU,
  output EPC,
  output End
);


  assign EB = Start;
  assign End = Start;
  assign EPC = Start;
  assign SA = 2'b00;
  assign SALU = 4'b0000;
  assign SB = 2'b00;

  // Other names for the same wires on the sheet: St = Start

  // Notes on the sheet:
  //   Input
  //   Ground
  //   Output
endmodule

module j (
  input  Start,
  input  Clk,
  input  Rst,
  output [1:0] SA,
  output [1:0] SB,
  output EB,
  output [3:0] SALU,
  output EPC,
  output End
);

  Multiplexer #(.width(2), .disabled(0), .enable("false")) multiplexer_1 (
    .in0(2'b00), .in1(2'b10), .out(SA), .sel(Start));

  assign EB = 1'b0;
  assign End = Start;
  assign EPC = Start;
  assign SALU = 4'b0000;
  assign SB = 2'b00;

  // Other names for the same wires on the sheet: St = Start

  // Notes on the sheet:
  //   Input
  //   Ground
  //   Output
endmodule

module jr (
  input  Start,
  input  Clk,
  input  Rst,
  output [1:0] SA,
  output [1:0] SB,
  output EB,
  output ER,
  output [3:0] SALU,
  output EPC,
  output End
);

  Multiplexer #(.width(2), .disabled(0), .enable("false")) multiplexer_1 (
    .in0(2'b00), .in1(2'b01), .out(SA), .sel(Start));

  assign EB = 1'b0;
  assign End = Start;
  assign EPC = Start;
  assign ER = Start;
  assign SALU = 4'b0000;
  assign SB = 2'b00;

  // Other names for the same wires on the sheet: St = Start

  // Notes on the sheet:
  //   Input
  //   Ground
  //   Output
endmodule

module IALU (
  input  Start,
  input  Clk,
  input  Rst,
  input  [3:0] SALU,
  output ER,
  output [1:0] SA,
  output [1:0] SB,
  output EB,
  output SWA,
  output SIS,
  output [3:0] SALU_2,
  output EALU,
  output [1:0] SW,
  output EW,
  output End
);

  wire comparator_1_lt;
  wire [3:0] SALU_t;

  Multiplexer #(.select(3), .width(4), .disabled(0), .enable("false")) multiplexer_1 (
    .in0(4'b0000), .in1(4'b0110), .in2(4'b0111), .in3(4'b0010), .in4(4'b0011), .in5(4'b0101), .in6(4'b0000),
    .in7(4'b0000), .out(SALU_t), .sel(SALU[2:0]));
  Comparator #(.width(4), .mode("unsigned")) comparator_1 (
    .a(4'b0010), .b(SALU), .lt(comparator_1_lt));  // open: gt, eq
  Multiplexer #(.width(2), .disabled(0), .enable("false")) multiplexer_2 (
    .in0(2'b00), .in1(2'b01), .out(SA), .sel(Start));
  Multiplexer #(.width(2), .disabled(0), .enable("false")) multiplexer_3 (
    .in0(2'b00), .in1(2'b10), .out(SB), .sel(Start));
  and and_1 (SIS, comparator_1_lt, Start);
  Multiplexer #(.width(4), .disabled(0), .enable("false")) multiplexer_4 (
    .in0(4'b0000), .in1(SALU_t), .out(SALU_2), .sel(Start));

  assign EALU = Start;
  assign EB = Start;
  assign End = Start;
  assign ER = Start;
  assign EW = Start;
  assign SW = 2'b00;
  assign SWA = Start;

  // Other names for the same wires on the sheet: OS[3:0] = SALU; St = Start

  // Notes on the sheet:
  //   Input
  //   Ground
  //   Output
endmodule

module Ibf (
  input  Start,
  input  Clk,
  input  Rst,
  input  [3:0] OS,
  input  ZF,
  input  NF,
  output ER,
  output [1:0] SA,
  output [1:0] SB,
  output EB,
  output [3:0] SALU,
  output EALU,
  output EPC,
  output End
);

  wire and_1_out, comparator_1_lt, comparator_2_eq, comparator_3_eq, comparator_4_eq, comparator_5_eq,
       comparator_6_eq, decoder_1_out1, End0, ISI4, not_1_out, not_2_out, or_3_out;
  wire [1:0] multiplexer_2_out;
  wire [2:0] S;

  Comparator #(.width(3), .mode("unsigned")) comparator_1 (.a(S), .b(3'b010), .lt(comparator_1_lt));  // open: gt, eq
  Multiplexer #(.width(2), .disabled(0), .enable("false")) multiplexer_1 (
    .in0(2'b00), .in1(2'b01), .out(SA), .sel(Start));
  Multiplexer #(.width(2), .disabled(0), .enable("false")) multiplexer_2 (
    .in0(2'b00), .in1(2'b01), .out(multiplexer_2_out), .sel(Start));
  and and_1 (and_1_out, Start, comparator_1_lt);
  or or_1 (EB, and_1_out, EPC);
  Multiplexer #(.width(4), .disabled(0), .enable("false")) multiplexer_3 (
    .in0(4'b0000), .in1(4'b0001), .out(SALU), .sel(Start));
  or or_2 (End, End0, EPC);
  Multiplexer #(.width(2), .disabled(0), .enable("false")) multiplexer_4 (
    .in0(multiplexer_2_out), .in1(2'b11), .out(SB), .sel(EPC));
  Comparator #(.width(4), .mode("unsigned")) comparator_2 (.a(OS), .b(4'b0110), .eq(comparator_2_eq));  // open: gt, lt
  Comparator #(.width(4), .mode("unsigned")) comparator_3 (.a(OS), .b(4'b0111), .eq(comparator_3_eq));  // open: gt, lt
  Comparator #(.width(4), .mode("unsigned")) comparator_4 (.a(OS), .b(4'b1000), .eq(comparator_4_eq));  // open: gt, lt
  Comparator #(.width(4), .mode("unsigned")) comparator_5 (.a(OS), .b(4'b1001), .eq(comparator_5_eq));  // open: gt, lt
  Comparator #(.width(4), .mode("unsigned")) comparator_6 (.a(OS), .b(4'b1010), .eq(comparator_6_eq));  // open: gt, lt
  not not_1 (not_1_out, ZF);
  or or_3 (or_3_out, ZF, NF);
  not not_2 (not_2_out, or_3_out);
  Pull_Resistor pull_resistor_1 (.node(S));
  Priority_Encoder #(.disabled(0)) priority_encoder_1 (
    .in0(comparator_2_eq), .in1(comparator_3_eq), .in2(comparator_4_eq), .in3(comparator_5_eq),
    .in4(comparator_6_eq), .in5(1'b0), .in6(1'b0), .in7(1'b0), .out(S));  // open: en_in, gs, en_out
  Multiplexer #(.select(3), .disabled(0), .enable("false")) multiplexer_5 (
    .in0(ZF), .in1(not_1_out), .in2(or_3_out), .in3(not_2_out), .in4(NF), .in5(1'b0), .in6(1'b0), .in7(1'b0),
    .out(ISI4), .sel(S));
  Decoder #(.disabled(0)) decoder_1 (.out0(End0), .out1(decoder_1_out1), .sel(ISI4), .en(Start));
  D_Flip_Flop u_ISI4 (.clk(Clk), .D(decoder_1_out1), .Q(EPC), .reset(Rst));  // open: Qn, preset, en

  assign EALU = Start;
  assign ER = Start;

  // Other names for the same wires on the sheet: IS = EPC; St = Start

  // Notes on the sheet:
  //   Input
  //   Ground
  //   Output
  //   Check Operation
  //   Check Conditions
  //   New State
endmodule

module RbMfhi_lo (
  input  Start,
  input  Clk,
  input  Rst,
  input  [3:0] SOp,
  output [1:0] SW,
  output EW,
  output End
);

  wire [1:0] SW_t;

  Multiplexer #(.width(2), .enable("false")) multiplexer_1 (.in0(2'b11), .in1(2'b10), .out(SW_t), .sel(SOp[0]));
  Multiplexer #(.width(2), .disabled(0), .enable("false")) multiplexer_2 (
    .in0(2'b00), .in1(SW_t), .out(SW), .sel(Start));

  assign End = Start;
  assign EW = Start;

  // Other names for the same wires on the sheet: St = Start

  // Notes on the sheet:
  //   Input
  //   Selector
  //   Output
endmodule
